# Fritzing sketch tugas3 (saved by Fritzing 0.9.4)
breadboards: 1

parts:
  U1 = ESP32S-HiLetgo [part_number=ESP32S-HiLetgo]
  R1 = Photocell (LDR) [package=THT]
  R2 = Resistor [tolerance=±5% resistance=4.7k package="1206 [SMD]"]
  R3 = Resistor [tolerance=±5% resistance=6.8k package="1206 [SMD]"]
  J1 = Basic Servo

nets:
  N1: U1.GPIO36, J1.pulse
  GND: U1.GPIO35, U1.GND, R1.pin_0, J1.gnd
  VIN: U1.VIN, R2.Pin_0, R3.Pin_0, J1.vcc
  N2: R1.pin_1, R2.Pin_1, R3.Pin_1

custom parts:
  ESP32S-HiLetgo: HiLetgo ESP-WROOM-32 ESP32 ESP-32S Development Board 2.4GHz Dual-Mode WiFi + Bluetooth Dual Cores Microcontroller The ESP32 integrated with Antenna switches, RF Balun, power amplifiers, low-noise amplifiers, filters, and management modules, and the entire solution occupies the least area of PCB. 2.4 GHz Wi-Fi plus Bluetooth dual-mode chip, with TSMC Ultra-low power consumption 40nm technology,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
